# Fritzing sketch PANGTEIH PROJECT (saved by Fritzing 0.9.3b)
breadboards: 1

parts:
  Part1 = Arduino Uno (Rev3)
  920KV_Motor1 = DJI 920 KV Motor
  M1 = ESC
  R1 = Rotary Potentiometer (Small) [maximum_resistance=100kΩ package=THT]
  Power_plug2 = Power plug  # not connected

nets:
  N1: Part1.A0, R1.wiper
  N2: Part1.D9_PWM, M1.DATA
  N3: Part1.5V, R1.leg2
  GND: Part1.GND, M1.GND, R1.leg1
  N4: 920KV_Motor1.w, M1.W
  N5: 920KV_Motor1.v, M1.V
  N6: 920KV_Motor1.u, M1.U

notes:
  BLDC
  ESC
  POTEIOMETER
  UNO
  ADAPTER INPUT
  ADAPTER

custom parts:
  DJI 920 KV Motor: DJI Brushless Outrunner 2212/920K Motor F330-550
