# Fritzing sketch PipeSub_Kapcsolasi_Rajz_01 (saved by Fritzing 0.9.9b)

parts:
  J1 = Wago 221-415
  920KV_Motor2 = DJI 920 KV Motor
  920KV_Motor4 = DJI 920 KV Motor
  920KV_Motor1 = DJI 920 KV Motor
  Part1 = Arduino Uno (Rev3)
  M2 = ESC
  M4 = ESC
  920KV_Motor3 = DJI 920 KV Motor
  M3 = ESC
  Part2 = Arduino Uno (Rev3)
  U1 = MAX485 Breakout [chip_label=? package=THT]
  U2 = MAX485 Breakout [chip_label=? package=THT]
  BAT1 = 12 battery [package=battery]
  M1 = RioRand LM2596
  M5 = ESC
  J2 = Wago 221-415
  Water_Level_Sensor1 = Water Level Sensor
  S1 = Round Pushbutton
  U3 = SWITCH-SPST-2 [package=r_sw_th]
  M6 = 1 chan 5v relay module

nets:
  N1: J1.Pin_1, J1.Pin_2, J1.Pin_3, J1.Pin_4, J1.Pin_5, M1.Pin_1, S1.leg1, M6.pin_4
  N2: 920KV_Motor2.w, M3.W
  N3: 920KV_Motor2.v, M3.V
  N4: 920KV_Motor2.u, M3.U
  N5: 920KV_Motor4.w, M5.W
  N6: 920KV_Motor4.v, M5.V
  N7: 920KV_Motor4.u, M5.U
  N8: 920KV_Motor1.w, M2.W
  N9: 920KV_Motor1.v, M2.V
  N10: 920KV_Motor1.u, M2.U
  N11: Part1.A0, Water_Level_Sensor1.SIG
  N12: Part1.D10_PWM/SS, M5.DATA
  N13: Part1.D11_PWM/MOSI, M4.DATA
  GND: Part1.GND, M2.GND, M4.GND, M3.GND, Part2.GND, U1.GND, U2.GND, M1.Pin_4, M5.GND, Water_Level_Sensor1.GND, M6.pin_2
  N14: Part1.D0/RX, U1.RO
  N15: Part1.D1/TX, U1.DI
  N16: Part1.D2, U1.RE, U1.DE
  N17: Part1.D7, M6.pin_3
  3V3: Part1.3V3, U1.VCC
  5V: Part1.5V, Water_Level_Sensor1.VCC, M6.pin_1
  VIN: Part1.VIN, Part2.VIN, M1.Pin_3
  N18: M2.DATA, Part2.D10_PWM/SS
  N19: M4.U, 920KV_Motor3.u
  N20: M4.V, 920KV_Motor3.v
  N21: M4.W, 920KV_Motor3.w
  N22: M3.DATA, Part2.D11_PWM/MOSI
  N23: Part2.D0/RX, U2.RO
  N24: Part2.D1/TX, U2.DI
  N25: Part2.D2, U2.RE, U2.DE
  3V3_2: Part2.3V3, U2.VCC
  N26: BAT1.-, M1.Pin_2, J2.Pin_1, J2.Pin_2, J2.Pin_3, J2.Pin_4, J2.Pin_5
  N27: BAT1.+, U3.P
  N28: S1.leg0, U3.O, M6.pin_5

custom parts:
  Wago 221-415: Wago 221-415 5 position splicing connector 12AWG.
  DJI 920 KV Motor: DJI Brushless Outrunner 2212/920K Motor F330-550
  MAX485 Breakout: MAX485 RS485 breakout board
  12 battery: 12V lead acid type battery, like the Husqvarna YTH2448 12V 35AH battery. This is the mini version 1/4 the size of the actual battery to be closer to typical breadboard parts (around 2in wide rathher than 7in). The pads in pcb are sized to accomidate up to 14ga wire (as these batterys will deliver high currents.)
  Water Level Sensor: A water level sensor. This sensor operates at 3V to 5V. The Sig (signal) pin outputs an analogue signal that is in proportion to the amount of water in contact with the sensor.
  1 chan 5v relay module: 1 Channel 5V Relay Module Board Shield with Optocoupler Support High and Low Level Trigger for Arduino.
