# Fritzing sketch PipeSub_Kapcsolasi_Rajz_02 (saved by Fritzing 0.9.9b)

parts:
  Part1 = Arduino Uno (Rev3)
  Part2 = Arduino Uno (Rev3)
  U1 = MAX485 Breakout [chip_label=? package=THT]
  U2 = MAX485 Breakout [chip_label=? package=THT]
  M1 = RioRand LM2596
  Part3 = Arduino Joystick Shield
  Part4 = Arduino Joystick Shield
  OLED_I2C1 = OLED 128x64 I2C Monochrome Display
  OLED_I2C2 = OLED 128x64 I2C Monochrome Display
  BAT1 = 12 battery [package=battery]

nets:
  GND: Part1.GND, Part2.GND, M1.Pin_3
  N1: Part1.VIN, M1.Pin_4
  N2: U1.RO, Part4.RX
  N3: U1.RE, U1.DE, Part4.SEL
  N4: U1.DI, Part4.TX
  VCC: U1.VCC, U2.VCC, OLED_I2C1.VDD, OLED_I2C2.VDD
  GND_2: U1.GND, U2.GND, OLED_I2C1.GND, OLED_I2C2.GND
  N5: U2.RO, Part3.RX
  N6: U2.RE, U2.DE, Part3.SEL
  N7: U2.DI, Part3.TX
  N8: M1.Pin_1, BAT1.-
  N9: M1.Pin_2, BAT1.+
  N10: Part3.A4, OLED_I2C1.SDA
  N11: Part3.A5, OLED_I2C1.SCK
  N12: Part4.A4, OLED_I2C2.SDA
  N13: Part4.A5, OLED_I2C2.SCK

custom parts:
  MAX485 Breakout: MAX485 RS485 breakout board
  12 battery: 12V lead acid type battery, like the Husqvarna YTH2448 12V 35AH battery. This is the mini version 1/4 the size of the actual battery to be closer to typical breadboard parts (around 2in wide rathher than 7in). The pads in pcb are sized to accomidate up to 14ga wire (as these batterys will deliver high currents.)
